// Logisim project Add2bit.circ as structural Verilog: 5 circuits, main circuit main
module main (
  input  A,
  input  B,
  output Y,
  output Z,
  output X
);

  wire and_1_out, and_2_out, not_1_out, not_2_out;

  nand nand_1 (Y, A, B);
  not not_1 (not_1_out, A);
  not not_2 (not_2_out, B);
  and and_1 (and_1_out, not_1_out, B);
  and and_2 (and_2_out, A, not_2_out);
  xor xor_1 (X, A, B);
  or or_1 (Z, and_1_out, and_2_out);
endmodule

module FA (
  input  A,
  input  B,
  input  Cin,
  output Sum,
  output Carry
);

  wire and_1_out, and_2_out, and_3_out, and_4_out, and_5_out, and_6_out, and_7_out, not_1_out, not_2_out,
       not_3_out, not_4_out;

  not not_1 (not_1_out, A);
  not not_2 (not_2_out, A);
  not not_3 (not_3_out, B);
  not not_4 (not_4_out, Cin);
  and and_1 (and_1_out, B, Cin);
  and and_2 (and_2_out, A, Cin);
  and and_3 (and_3_out, A, B);
  and and_4 (and_4_out, not_1_out, Cin);
  and and_5 (and_5_out, not_2_out, B);
  and and_6 (and_6_out, B, Cin);
  and and_7 (and_7_out, A, not_3_out, not_4_out);
  or or_1 (Carry, and_1_out, and_2_out, and_3_out);
  or or_2 (Sum, and_4_out, and_5_out, and_6_out, and_7_out);
endmodule

module Add2bit (
  input  A0,
  input  A1,
  input  B0,
  input  B1,
  output S0,
  output S1,
  output Cout
);

  wire fa_1_carry;

  FA fa_1 (.A(A0), .B(B0), .Cin(1'b0), .Sum(S0), .Carry(fa_1_carry));
  FA fa_2 (.A(A1), .B(B1), .Cin(fa_1_carry), .Sum(S1), .Carry(Cout));
  LED led_1 (.in(S1));
endmodule

module desain_rangk_sekuensial (
  input  A,
  input  B,
  input  Clock,
  output C,
  output out_5
);

  wire and_1_out, nor_1_out, xor_1_out, xor_2_out;

  and and_1 (and_1_out, A, B);
  nor nor_1 (nor_1_out, A, B);
  S_R_Flip_Flop #(.trigger("falling")) s_r_ff_1 (
    .S(and_1_out), .clk(Clock), .R(nor_1_out), .Q(C));  // open: Qn, preset, reset, en
  xor xor_1 (xor_1_out, C, A);
  xor xor_2 (xor_2_out, xor_1_out, B);
  D_Flip_Flop d_ff_1 (.clk(Clock), .D(xor_2_out), .Q(out_5));  // open: Qn, preset, en, reset
endmodule

module counter (
  output out_1,
  output out_2,
  output out_3,
  output out_4
);

  wire clock_1_out;

  T_Flip_Flop t_ff_1 (.clk(out_2), .T(1'b1), .Q(out_1));  // open: Qn, preset, reset, en
  T_Flip_Flop t_ff_2 (.clk(out_3), .T(1'b1), .Q(out_2));  // open: Qn, preset, reset, en
  T_Flip_Flop t_ff_3 (.clk(out_4), .T(1'b1), .Q(out_3));  // open: Qn, preset, reset, en
  Clock clock_1 (.out(clock_1_out));
  T_Flip_Flop t_ff_4 (.clk(clock_1_out), .T(1'b1), .Q(out_4));  // open: Qn, preset, reset, en
endmodule
