// Logisim project assesmentram.circ as structural Verilog: 8 circuits, main circuit main
module main (
  input  in_1,
  input  in_2,
  input  in_3,
  input  in_4,
  input  in_5,
  input  in_6,
  input  in_7,
  input  in_8,
  input  [7:0] in_9,
  input  in_10,
  input  in_11,
  input  in_12,
  input  Jumlah,
  input  Kurang
);

  wire [7:0] _1_out_2, _2_out_2, _3_out_2, acumulator_1_out_2, alu_1_hasil_jumlah, alu_1_hasil_kurang,
       controlled_buffer_1_out, controlled_buffer_5_out, controlled_buffer_6_out, controlled_buffer_7_out,
       controlled_buffer_9_out, controlled_buffer_10_out, controlled_buffer_11_out, controlled_buffer_12_out,
       Q_out_2, x_1_out_2;

  // Probe on x_1_out_2
  // Probe on Q_out_2
  assign controlled_buffer_1_out = in_1 ? Q_out_2 : 8'bz;  // Controlled_Buffer controlled_buffer_1
  // Probe on _1_out_2
  assign controlled_buffer_1_out = in_3 ? _1_out_2 : 8'bz;  // Controlled_Buffer controlled_buffer_2
  // Probe on _2_out_2
  assign controlled_buffer_1_out = in_5 ? _2_out_2 : 8'bz;  // Controlled_Buffer controlled_buffer_3
  // Probe on _3_out_2
  assign controlled_buffer_1_out = in_7 ? _3_out_2 : 8'bz;  // Controlled_Buffer controlled_buffer_4
  assign controlled_buffer_5_out = in_12 ? x_1_out_2 : 8'bz;  // Controlled_Buffer controlled_buffer_5
  X x_1 (.in_1(controlled_buffer_1_out), .out_2(x_1_out_2));
  // Probe on controlled_buffer_9_out
  register Q (.in_1(controlled_buffer_9_out), .out_2(Q_out_2));
  // Probe on controlled_buffer_10_out
  register _1 (.in_1(controlled_buffer_10_out), .out_2(_1_out_2));
  // Probe on controlled_buffer_11_out
  register _2 (.in_1(controlled_buffer_11_out), .out_2(_2_out_2));
  // Probe on controlled_buffer_12_out
  register _3 (.in_1(controlled_buffer_12_out), .out_2(_3_out_2));
  assign controlled_buffer_6_out = in_11 ? acumulator_1_out_2 : 8'bz;  // Controlled_Buffer controlled_buffer_6
  ALU alu_1 (
    .in_1(controlled_buffer_6_out), .in_2(controlled_buffer_5_out), .Hasil_Jumlah(alu_1_hasil_jumlah),
    .Hasil_kurang(alu_1_hasil_kurang));
  assign controlled_buffer_7_out = Jumlah ? alu_1_hasil_jumlah : 8'bz;  // Controlled_Buffer controlled_buffer_7
  assign controlled_buffer_7_out = Kurang ? alu_1_hasil_kurang : 8'bz;  // Controlled_Buffer controlled_buffer_8
  assign controlled_buffer_9_out = in_2 ? acumulator_1_out_2 : 8'bz;  // Controlled_Buffer controlled_buffer_9
  Controlled_Buffer #(.width(8)) controlled_buffer_10 (.out(controlled_buffer_10_out), .en(in_4));  // open: in
  Controlled_Buffer #(.width(8)) controlled_buffer_11 (.out(controlled_buffer_11_out), .en(in_6));  // open: in
  Controlled_Buffer #(.width(8)) controlled_buffer_12 (.out(controlled_buffer_12_out), .en(in_8));  // open: in
  // Probe on acumulator_1_out_2
  Acumulator acumulator_1 (.in_1(controlled_buffer_7_out), .out_2(acumulator_1_out_2));
  // Probe on in_9
  assign controlled_buffer_7_out = in_10 ? in_9 : 8'bz;  // Controlled_Buffer controlled_buffer_13
  // Probe on controlled_buffer_7_out
endmodule

// equ
module SUM (
  input  [7:0] in_1,
  input  [7:0] in_2,
  output [7:0] out_3
);

  // Probe on in_1
  // Probe on in_2
  Adder adder_1 (.a(in_1), .b(in_2), .out(out_3));  // open: cin, cout
  // Probe on out_3
endmodule

// SUM
module equlity (
  input  [7:0] in_1,
  input  [7:0] in_2,
  output [7:0] out_3
);

  // Probe on in_1
  // Probe on in_2
  // Probe on out_3
  Subtractor subtractor_1 (.a(in_1), .b(in_2), .out(out_3));  // open: bin, bout
endmodule

module ALU (
  input  [7:0] in_1,
  input  [7:0] in_2,
  output [7:0] Hasil_Jumlah,
  output [7:0] Hasil_kurang
);

  // Probe on in_1
  // Probe on in_2
  SUM sum_1 (.in_1(in_2), .in_2(in_1), .out_3(Hasil_Jumlah));
  equlity equlity_1 (.in_1(in_1), .in_2(in_2), .out_3(Hasil_kurang));
  // Probe on Hasil_Jumlah
  // Probe on Hasil_kurang
endmodule

// R
module register (
  input  [7:0] in_1,
  output [7:0] out_2
);

  wire clock_1_out;

  Clock clock_1 (.out(clock_1_out));
  // Probe on {{2{in_1[7]}}, in_1[5:0]}
  D_Flip_Flop d_ff_1 (.clk(clock_1_out), .D(in_1[0]), .Q(out_2[0]));  // open: Qn, preset, en, reset
  D_Flip_Flop d_ff_2 (.clk(clock_1_out), .D(in_1[1]), .Q(out_2[1]));  // open: Qn, preset, en, reset
  D_Flip_Flop d_ff_3 (.clk(clock_1_out), .D(in_1[2]), .Q(out_2[2]));  // open: Qn, preset, en, reset
  D_Flip_Flop d_ff_4 (.clk(clock_1_out), .D(in_1[3]), .Q(out_2[3]));  // open: Qn, preset, en, reset
  D_Flip_Flop d_ff_5 (.clk(clock_1_out), .D(in_1[4]), .Q(out_2[4]));  // open: Qn, preset, en, reset
  D_Flip_Flop d_ff_6 (.clk(clock_1_out), .D(in_1[5]), .Q(out_2[5]));  // open: Qn, preset, en, reset
  D_Flip_Flop d_ff_7 (.clk(clock_1_out), .D(in_1[7]), .Q(out_2[6]));  // open: Qn, preset, en, reset
  D_Flip_Flop d_ff_8 (.clk(clock_1_out), .D(in_1[7]), .Q(out_2[7]));  // open: Qn, preset, en, reset
  // Probe on out_2

  assign in_1[6] = in_1[7];
endmodule

module X (
  input  [7:0] in_1,
  output [7:0] out_2
);

  wire clock_1_out;

  Clock clock_1 (.out(clock_1_out));
  // Probe on {{2{in_1[7]}}, in_1[5:0]}
  D_Flip_Flop d_ff_1 (.clk(clock_1_out), .D(in_1[0]), .Q(out_2[0]));  // open: Qn, preset, en, reset
  D_Flip_Flop d_ff_2 (.clk(clock_1_out), .D(in_1[1]), .Q(out_2[1]));  // open: Qn, preset, en, reset
  D_Flip_Flop d_ff_3 (.clk(clock_1_out), .D(in_1[2]), .Q(out_2[2]));  // open: Qn, preset, en, reset
  D_Flip_Flop d_ff_4 (.clk(clock_1_out), .D(in_1[3]), .Q(out_2[3]));  // open: Qn, preset, en, reset
  D_Flip_Flop d_ff_5 (.clk(clock_1_out), .D(in_1[4]), .Q(out_2[4]));  // open: Qn, preset, en, reset
  D_Flip_Flop d_ff_6 (.clk(clock_1_out), .D(in_1[5]), .Q(out_2[5]));  // open: Qn, preset, en, reset
  D_Flip_Flop d_ff_7 (.clk(clock_1_out), .D(in_1[7]), .Q(out_2[6]));  // open: Qn, preset, en, reset
  D_Flip_Flop d_ff_8 (.clk(clock_1_out), .D(in_1[7]), .Q(out_2[7]));  // open: Qn, preset, en, reset
  // Probe on out_2

  assign in_1[6] = in_1[7];
endmodule

module Y (
  input  [7:0] in_1,
  output [7:0] out_2
);

  wire clock_1_out;

  Clock clock_1 (.out(clock_1_out));
  // Probe on {{2{in_1[7]}}, in_1[5:0]}
  D_Flip_Flop d_ff_1 (.clk(clock_1_out), .D(in_1[0]), .Q(out_2[0]));  // open: Qn, preset, en, reset
  D_Flip_Flop d_ff_2 (.clk(clock_1_out), .D(in_1[1]), .Q(out_2[1]));  // open: Qn, preset, en, reset
  D_Flip_Flop d_ff_3 (.clk(clock_1_out), .D(in_1[2]), .Q(out_2[2]));  // open: Qn, preset, en, reset
  D_Flip_Flop d_ff_4 (.clk(clock_1_out), .D(in_1[3]), .Q(out_2[3]));  // open: Qn, preset, en, reset
  D_Flip_Flop d_ff_5 (.clk(clock_1_out), .D(in_1[4]), .Q(out_2[4]));  // open: Qn, preset, en, reset
  D_Flip_Flop d_ff_6 (.clk(clock_1_out), .D(in_1[5]), .Q(out_2[5]));  // open: Qn, preset, en, reset
  D_Flip_Flop d_ff_7 (.clk(clock_1_out), .D(in_1[7]), .Q(out_2[6]));  // open: Qn, preset, en, reset
  D_Flip_Flop d_ff_8 (.clk(clock_1_out), .D(in_1[7]), .Q(out_2[7]));  // open: Qn, preset, en, reset
  // Probe on out_2

  assign in_1[6] = in_1[7];
endmodule

// A
module Acumulator (
  input  [7:0] in_1,
  output [7:0] out_2
);

  wire clock_1_out;

  Clock clock_1 (.out(clock_1_out));
  // Probe on {{2{in_1[7]}}, in_1[5:0]}
  D_Flip_Flop d_ff_1 (.clk(clock_1_out), .D(in_1[0]), .Q(out_2[0]));  // open: Qn, preset, en, reset
  D_Flip_Flop d_ff_2 (.clk(clock_1_out), .D(in_1[1]), .Q(out_2[1]));  // open: Qn, preset, en, reset
  D_Flip_Flop d_ff_3 (.clk(clock_1_out), .D(in_1[2]), .Q(out_2[2]));  // open: Qn, preset, en, reset
  D_Flip_Flop d_ff_4 (.clk(clock_1_out), .D(in_1[3]), .Q(out_2[3]));  // open: Qn, preset, en, reset
  D_Flip_Flop d_ff_5 (.clk(clock_1_out), .D(in_1[4]), .Q(out_2[4]));  // open: Qn, preset, en, reset
  D_Flip_Flop d_ff_6 (.clk(clock_1_out), .D(in_1[5]), .Q(out_2[5]));  // open: Qn, preset, en, reset
  D_Flip_Flop d_ff_7 (.clk(clock_1_out), .D(in_1[7]), .Q(out_2[6]));  // open: Qn, preset, en, reset
  D_Flip_Flop d_ff_8 (.clk(clock_1_out), .D(in_1[7]), .Q(out_2[7]));  // open: Qn, preset, en, reset
  // Probe on out_2

  assign in_1[6] = in_1[7];
endmodule
