// Logisim project latihan 5.circ as structural Verilog: 11 circuits, main circuit main
module main (
  input  [7:0] in_1,
  input  [7:0] in_2,
  output [15:0] out_3
);

  // Probe on in_1
  // Probe on in_2
  // Probe on out_3
  mult8 mult8_1 (.A(in_1), .B(in_2), .out(out_3));
endmodule

module Controller (
  input  U
);

  wire clock_1_out, eksitasi_1_tx, eksitasi_1_ty, eksitasi_1_tz, output_1_a, output_1_b, output_1_c,
       output_1_d, output_1_e, X_q, Y_q, Z_q;

  Clock clock_1 (.out(clock_1_out));
  eksitasi eksitasi_1 (.U(U), .X(X_q), .Y(Y_q), .Z(Z_q), .Tx(eksitasi_1_tx), .Ty(eksitasi_1_ty), .Tz(eksitasi_1_tz));
  T_Flip_Flop X (.clk(clock_1_out), .T(eksitasi_1_tx), .Q(X_q));  // open: Qn, preset, reset, en
  T_Flip_Flop Y (.clk(clock_1_out), .T(eksitasi_1_ty), .Q(Y_q));  // open: Qn, preset, reset, en
  T_Flip_Flop Z (.clk(clock_1_out), .T(eksitasi_1_tz), .Q(Z_q));  // open: Qn, preset, reset, en
  \output  output_1 (
    .U(U), .X(X_q), .Y(Y_q), .Z(Z_q), .A(output_1_a), .B(output_1_b), .C(output_1_c), .D(output_1_d),
    .E(output_1_e));
  LED led_1 (.in(output_1_a));
  LED led_2 (.in(output_1_a));
  LED led_3 (.in(output_1_e));
  LED led_4 (.in(output_1_e));
  LED led_5 (.in(output_1_b));
  LED led_6 (.in(1'b1));
  LED led_7 (.in(output_1_c));
  LED led_8 (.in(output_1_d));
  LED led_9 (.in(output_1_d));
  LED led_10 (.in(output_1_b));
  LED led_11 (.in(output_1_c));
endmodule

module eksitasi (
  input  U,
  input  X,
  input  Y,
  input  Z,
  output Tx,
  output Ty,
  output Tz
);

  wire and_1_out, and_2_out, and_3_out, and_4_out, and_5_out, and_6_out, and_7_out, and_8_out, and_9_out,
       not_1_out, not_2_out, not_3_out, not_4_out, not_5_out, not_6_out, not_7_out, not_8_out, not_9_out,
       not_10_out, not_11_out;

  not not_1 (not_1_out, U);
  and and_1 (and_1_out, not_1_out, Y, Z);
  not not_2 (not_2_out, Y);
  and and_2 (and_2_out, U, not_2_out, not_3_out);
  not not_3 (not_3_out, Z);
  not not_4 (not_4_out, U);
  and and_3 (and_3_out, not_4_out, not_5_out, Z);
  not not_5 (not_5_out, X);
  and and_4 (and_4_out, X, Y);
  and and_5 (and_5_out, U, Y, not_6_out);
  not not_6 (not_6_out, Z);
  and and_6 (and_6_out, U, X, not_7_out);
  not not_7 (not_7_out, Z);
  not not_8 (not_8_out, U);
  and and_7 (and_7_out, not_8_out, not_9_out);
  not not_9 (not_9_out, X);
  not not_10 (not_10_out, X);
  and and_8 (and_8_out, not_10_out, Y);
  and and_9 (and_9_out, U, X, not_11_out);
  not not_11 (not_11_out, Y);
  or or_1 (Tx, and_1_out, X, and_2_out);
  or or_2 (Ty, and_3_out, and_4_out, and_5_out, and_6_out);
  or or_3 (Tz, and_7_out, Z, and_8_out, and_9_out);
endmodule

module \output  (
  input  U,
  input  X,
  input  Y,
  input  Z,
  output A,
  output B,
  output C,
  output D,
  output E
);

  wire and_1_out, and_2_out, and_3_out, not_1_out, not_2_out, not_3_out, not_4_out, not_5_out, not_6_out,
       not_7_out, not_8_out, not_9_out, not_10_out;

  not not_1 (not_1_out, X);
  not not_2 (not_2_out, Y);
  and and_1 (and_1_out, not_1_out, not_2_out, not_3_out);
  not not_3 (not_3_out, Z);
  and and_2 (and_2_out, X, Z);
  and and_3 (and_3_out, X, Y);
  not not_4 (not_4_out, X);
  not not_5 (not_5_out, Y);
  and and_4 (B, not_4_out, not_5_out, Z);
  not not_6 (not_6_out, X);
  and and_5 (C, not_6_out, Y, not_7_out);
  not not_7 (not_7_out, Z);
  not not_8 (not_8_out, X);
  and and_6 (D, not_8_out, Y, Z);
  not not_9 (not_9_out, Y);
  and and_7 (E, X, not_9_out, not_10_out);
  not not_10 (not_10_out, Z);
  or or_1 (A, and_1_out, and_2_out, and_3_out);
endmodule

module shift_reg (
  input  in,
  input  S
);

  wire A_q, and_1_out, and_2_out, and_3_out, and_4_out, B_q, C_q, clock_1_out, D_q, E_q, not_1_out, or_1_out,
       or_2_out;

  Clock clock_1 (.out(clock_1_out));
  or or_1 (or_1_out, and_1_out, and_3_out);
  and and_1 (and_1_out, not_1_out, B_q);
  not not_1 (not_1_out, S);
  D_Flip_Flop A (.clk(clock_1_out), .D(or_1_out), .Q(A_q));  // open: Qn, preset, en, reset
  and and_2 (and_2_out, not_1_out, C_q);
  and and_3 (and_3_out, S, in);
  D_Flip_Flop B (.clk(clock_1_out), .D(or_2_out), .Q(B_q));  // open: Qn, preset, en, reset
  or or_2 (or_2_out, and_2_out, and_4_out);
  and and_4 (and_4_out, A_q, S);
  D_Flip_Flop C (.clk(clock_1_out), .D(D_q), .Q(C_q));  // open: Qn, preset, en, reset
  D_Flip_Flop D (.clk(clock_1_out), .D(E_q), .Q(D_q));  // open: Qn, preset, en, reset
  D_Flip_Flop E (.clk(clock_1_out), .D(in), .Q(E_q));  // open: Qn, preset, en, reset
endmodule

// R
module register (
  input  Load,
  input  [7:0] D,
  output [7:0] Q
);

  D_Flip_Flop d_ff_1 (.clk(Load), .D(D[0]), .Q(Q[0]));  // open: Qn, preset, en, reset
  D_Flip_Flop d_ff_2 (.clk(Load), .D(D[1]), .Q(Q[1]));  // open: Qn, preset, en, reset
  D_Flip_Flop d_ff_3 (.clk(Load), .D(D[2]), .Q(Q[2]));  // open: Qn, preset, en, reset
  D_Flip_Flop d_ff_4 (.clk(Load), .D(D[3]), .Q(Q[3]));  // open: Qn, preset, en, reset
  D_Flip_Flop d_ff_5 (.clk(Load), .D(D[4]), .Q(Q[4]));  // open: Qn, preset, en, reset
  D_Flip_Flop d_ff_6 (.clk(Load), .D(D[5]), .Q(Q[5]));  // open: Qn, preset, en, reset
  D_Flip_Flop d_ff_7 (.clk(Load), .D(D[6]), .Q(Q[6]));  // open: Qn, preset, en, reset
  D_Flip_Flop d_ff_8 (.clk(Load), .D(D[7]), .Q(Q[7]));  // open: Qn, preset, en, reset
endmodule

module more_reg (
  input  LA,
  input  LB,
  input  LC,
  input  OA,
  input  OB,
  input  OC,
  output [7:0] out_7,
  output [7:0] out_8,
  output [7:0] out_9,
  output [7:0] out_10
);

  register register_1 (.Load(LA), .D(out_10), .Q(out_7));
  register register_2 (.Load(LB), .D(out_10), .Q(out_8));
  register register_3 (.Load(LC), .D(out_10), .Q(out_9));
  // Probe on out_7
  // Probe on out_10
  assign out_10 = OA ? out_7 : 8'bz;  // Controlled_Buffer controlled_buffer_1
  assign out_10 = OB ? out_8 : 8'bz;  // Controlled_Buffer controlled_buffer_2
  assign out_10 = OC ? out_9 : 8'bz;  // Controlled_Buffer controlled_buffer_3
endmodule

// M88
module mult8 (
  input  [7:0] A,
  input  [7:0] B,
  output [15:0] out
);

  wire mul8_add_1_cout, mul8_add_2_cout, mul8_add_3_cout, mul8_add_4_cout, mul8_add_5_cout, mul8_add_6_cout;
  wire [7:0] mul8_1_1_out, mul8_1_2_out, mul8_1_3_out, mul8_1_4_out, mul8_1_5_out, mul8_1_6_out,
       mul8_1_7_out, mul8_1_8_out, mul8_add_1_out8, mul8_add_2_out8, mul8_add_3_out8, mul8_add_4_out8,
       mul8_add_5_out8, mul8_add_6_out8;

  mul8_1 mul8_1_1 (.A(A), .B(B[0]), .Out(mul8_1_1_out));
  mul8_1 mul8_1_2 (.A(A), .B(B[1]), .Out(mul8_1_2_out));
  mul8_1 mul8_1_3 (.A(A), .B(B[2]), .Out(mul8_1_3_out));
  mul8_1 mul8_1_4 (.A(A), .B(B[3]), .Out(mul8_1_4_out));
  mul8_1 mul8_1_5 (.A(A), .B(B[4]), .Out(mul8_1_5_out));
  mul8_1 mul8_1_6 (.A(A), .B(B[5]), .Out(mul8_1_6_out));
  mul8_1 mul8_1_7 (.A(A), .B(B[6]), .Out(mul8_1_7_out));
  mul8_1 mul8_1_8 (.A(A), .B(B[7]), .Out(mul8_1_8_out));
  mul8_add mul8_add_1 (
    .Cin(1'b0), .A(mul8_1_1_out), .B(mul8_1_2_out), .B0(out[0]), .Out8(mul8_add_1_out8),
    .Cout(mul8_add_1_cout));
  mul8_add mul8_add_2 (
    .Cin(mul8_add_1_cout), .A(mul8_add_1_out8), .B(mul8_1_3_out), .B0(out[1]), .Out8(mul8_add_2_out8),
    .Cout(mul8_add_2_cout));
  mul8_add mul8_add_3 (
    .Cin(mul8_add_2_cout), .A(mul8_add_2_out8), .B(mul8_1_4_out), .B0(out[2]), .Out8(mul8_add_3_out8),
    .Cout(mul8_add_3_cout));
  mul8_add mul8_add_4 (
    .Cin(mul8_add_3_cout), .A(mul8_add_3_out8), .B(mul8_1_5_out), .B0(out[3]), .Out8(mul8_add_4_out8),
    .Cout(mul8_add_4_cout));
  mul8_add mul8_add_5 (
    .Cin(mul8_add_4_cout), .A(mul8_add_4_out8), .B(mul8_1_6_out), .B0(out[4]), .Out8(mul8_add_5_out8),
    .Cout(mul8_add_5_cout));
  mul8_add mul8_add_6 (
    .Cin(mul8_add_5_cout), .A(mul8_add_5_out8), .B(mul8_1_7_out), .B0(out[5]), .Out8(mul8_add_6_out8),
    .Cout(mul8_add_6_cout));
  mul8_add mul8_add_7 (
    .Cin(mul8_add_6_cout), .A(mul8_add_6_out8), .B(mul8_1_8_out), .B0(out[6]), .Out8(out[14:7]),
    .Cout(out[15]));
endmodule

// Add
module mul8_add (
  input  Cin,
  input  [7:0] A,
  input  [7:0] B,
  output B0,
  output [7:0] Out8,
  output Cout
);

  Adder adder_1 (.a({Cin, A[7:1]}), .b(B), .out(Out8), .cout(Cout));  // open: cin

  assign B0 = A[0];
endmodule

// M81
module mul8_1 (
  input  [7:0] A,
  input  B,
  output [7:0] Out
);

  assign Out = A & {8{B}};  // AND_Gate and_1, 8 bits wide
endmodule

module CPU (
  input  in_1,
  input  in_2,
  input  in_3,
  input  in_4,
  input  in_5,
  input  in_6,
  input  in_7,
  input  in_8,
  input  in_9,
  input  in_10,
  input  in_11,
  input  in_12,
  input  in_13,
  input  in_14,
  input  in_15,
  input  in_16,
  input  in_17,
  input  in_18,
  input  in_19,
  input  in_20,
  input  in_21,
  input  in_22,
  input  in_23
);

  wire decoder_1_out0, decoder_1_out1;
  wire [7:0] A_q, adder_1_out, B_q, C_q, controlled_buffer_1_out, controlled_buffer_6_out,
       controlled_buffer_8_out, controlled_buffer_12_out, D_q, MAR_q, MDR_q, PC_q, rom_1_data;

  register A (.Load(in_1), .D(controlled_buffer_1_out), .Q(A_q));
  register B (.Load(in_5), .D(controlled_buffer_1_out), .Q(B_q));
  register C (.Load(in_10), .D(controlled_buffer_1_out), .Q(C_q));
  register D (.Load(in_16), .D(controlled_buffer_1_out), .Q(D_q));
  // Probe on controlled_buffer_1_out
  assign controlled_buffer_1_out = in_2 ? A_q : 8'bz;  // Controlled_Buffer controlled_buffer_1
  assign controlled_buffer_1_out = in_8 ? B_q : 8'bz;  // Controlled_Buffer controlled_buffer_2
  assign controlled_buffer_1_out = in_12 ? C_q : 8'bz;  // Controlled_Buffer controlled_buffer_3
  assign controlled_buffer_1_out = in_17 ? D_q : 8'bz;  // Controlled_Buffer controlled_buffer_4
  assign controlled_buffer_1_out = in_6 ? PC_q : 8'bz;  // Controlled_Buffer controlled_buffer_5
  assign controlled_buffer_6_out = in_9 ? controlled_buffer_1_out : 8'bz;  // Controlled_Buffer controlled_buffer_6
  assign controlled_buffer_6_out = in_11 ? adder_1_out : 8'bz;  // Controlled_Buffer controlled_buffer_7
  assign controlled_buffer_8_out = in_18 ? controlled_buffer_1_out : 8'bz;  // Controlled_Buffer controlled_buffer_8
  Register MAR (.D(controlled_buffer_1_out), .Q(MAR_q), .clk(in_3));  // open: en, clr
  Register PC (.D(controlled_buffer_6_out), .Q(PC_q), .clk(in_13));  // open: en, clr
  Register MDR (.D(controlled_buffer_8_out), .Q(MDR_q), .clk(in_21));  // open: en, clr
  Decoder #(.select(2), .enable("false")) decoder_1 (
    .out0(decoder_1_out0), .out1(decoder_1_out1), .sel(MAR_q[7:6]));  // open: out2, out3
  Adder adder_1 (.a(PC_q), .b(8'h1), .out(adder_1_out));  // open: cin, cout
  assign controlled_buffer_8_out = in_15 ? controlled_buffer_1_out : 8'bz;  // Controlled_Buffer controlled_buffer_9
  assign controlled_buffer_1_out = in_22 ? MDR_q : 8'bz;  // Controlled_Buffer controlled_buffer_10
  assign controlled_buffer_1_out = in_19 ? MDR_q : 8'bz;  // Controlled_Buffer controlled_buffer_11
  ROM #(.addrWidth(6)) rom_1 (.addr(MAR_q[5:0]), .data(rom_1_data), .sel(decoder_1_out0));
  assign controlled_buffer_12_out = in_7 ? controlled_buffer_1_out : 8'bz;  // Controlled_Buffer controlled_buffer_12
  RAM #(.addrWidth(6)) ram_1 (
    .addr(MAR_q[5:0]), .data(controlled_buffer_12_out), .sel(decoder_1_out1), .clk(in_20), .ld(in_23));  // open: clr
  assign controlled_buffer_1_out = in_4 ? rom_1_data : 8'bz;  // Controlled_Buffer controlled_buffer_13
  assign controlled_buffer_1_out = in_14 ? controlled_buffer_12_out : 8'bz;  // Controlled_Buffer controlled_buffer_14

  // Notes on the sheet:
  //   contents of rom_1 (hex, n*v repeats v):
  //   0 40 40
endmodule
