// Logisim project latihan2.circ as structural Verilog: 4 circuits, main circuit main
module main (
  input  D,
  input  C,
  input  B,
  output X,
  output Y
);

  wire and_1_out, and_2_out, not_1_out, not_2_out;

  not not_1 (not_1_out, D);
  and and_1 (and_1_out, not_1_out, C);
  not not_2 (not_2_out, C);
  and and_2 (and_2_out, not_1_out, not_2_out, B);
  or or_1 (X, D, and_1_out);
  or or_2 (Y, D, and_2_out);
endmodule

module multiplexer (
  input  X0,
  input  X1,
  input  X2,
  input  X3,
  input  S1,
  input  S0,
  output Y
);

  wire and_1_out, and_2_out, and_3_out, and_4_out, decoder_1_y0, decoder_1_y1, decoder_1_y2, decoder_1_y3;

  decoder decoder_1 (.A(S1), .B(S0), .Y0(decoder_1_y0), .Y1(decoder_1_y1), .Y2(decoder_1_y2), .Y3(decoder_1_y3));
  and and_1 (and_1_out, X0, decoder_1_y0);
  and and_2 (and_2_out, X1, decoder_1_y1);
  and and_3 (and_3_out, X2, decoder_1_y2);
  and and_4 (and_4_out, X3, decoder_1_y3);
  or or_1 (Y, and_1_out, and_2_out, and_3_out, and_4_out);
endmodule

module encoder (
  input  D,
  input  C,
  input  B,
  input  A,
  output X,
  output Y
);

  wire and_1_out, and_2_out, not_1_out, not_2_out;

  not not_1 (not_1_out, D);
  and and_1 (and_1_out, not_1_out, C);
  and and_2 (and_2_out, not_1_out, not_2_out, B);
  not not_2 (not_2_out, C);
  or or_1 (X, D, and_1_out);
  or or_2 (Y, D, and_2_out);
endmodule

module decoder (
  input  A,
  input  B,
  output Y0,
  output Y1,
  output Y2,
  output Y3
);

  wire not_1_out, not_2_out, not_3_out, not_4_out;

  not not_1 (not_1_out, A);
  not not_2 (not_2_out, B);
  not not_3 (not_3_out, A);
  not not_4 (not_4_out, B);
  and and_1 (Y3, A, B);
  and and_2 (Y0, not_1_out, not_2_out);
  and and_3 (Y1, not_3_out, B);
  and and_4 (Y2, A, not_4_out);
endmodule
