// Logisim project latihan4.circ as structural Verilog: 8 circuits, main circuit main
module main (
  input  i,
  output A,
  output B
);

  wire clock_1_out, not_1_out, xor_1_out, xor_2_out;

  Clock clock_1 (.out(clock_1_out));
  xor xor_1 (xor_1_out, i, xor_2_out);
  D_Flip_Flop u_A (.clk(clock_1_out), .D(xor_1_out), .Q(A));  // open: Qn, preset, en, reset
  D_Flip_Flop u_B (.clk(clock_1_out), .D(not_1_out), .Q(B));  // open: Qn, preset, en, reset
  not not_1 (not_1_out, B);
  xor xor_2 (xor_2_out, B, A);
endmodule

module Counter_4_bit (
  input  i,
  input  Clock,
  output A,
  output B,
  output C,
  output D
);

  wire da_1_da, db_1_db, dc_1_dc, dd_1_dd;

  D_Flip_Flop u_A (.clk(Clock), .D(da_1_da), .Q(A));  // open: Qn, preset, en, reset
  D_Flip_Flop u_B (.clk(Clock), .D(db_1_db), .Q(B));  // open: Qn, preset, en, reset
  D_Flip_Flop u_C (.clk(Clock), .D(dc_1_dc), .Q(C));  // open: Qn, preset, en, reset
  D_Flip_Flop u_D (.clk(Clock), .D(dd_1_dd), .Q(D));  // open: Qn, preset, en, reset
  DA da_1 (.i(i), .A(A), .B(B), .C(C), .D(D), .DA(da_1_da));
  DB db_1 (.i(i), .A(A), .B(B), .C(C), .D(D), .DB(db_1_db));
  DC dc_1 (.i(i), .A(A), .B(B), .C(C), .D(D), .DC(dc_1_dc));
  DD dd_1 (.i(i), .A(A), .B(B), .C(C), .D(D), .DD(dd_1_dd));
endmodule

module dg_TFF (
  input  i,
  output A,
  output B
);

  wire clock_1_out, xor_1_out;

  Clock clock_1 (.out(clock_1_out));
  xor xor_1 (xor_1_out, i, B);
  T_Flip_Flop u_A (.clk(clock_1_out), .T(xor_1_out), .Q(A));  // open: Qn, preset, reset, en
  T_Flip_Flop u_B (.clk(clock_1_out), .T(1'b1), .Q(B));  // open: Qn, preset, reset, en
endmodule

module DA (
  input  i,
  input  A,
  input  B,
  input  C,
  input  D,
  output DA
);

  wire and_1_out, and_2_out, and_3_out, and_4_out, and_5_out, and_6_out, and_7_out, not_1_out, not_2_out,
       not_3_out, not_4_out, not_5_out, not_6_out, not_7_out, not_8_out, not_9_out, not_10_out, not_11_out,
       not_12_out;

  not not_1 (not_1_out, i);
  not not_2 (not_2_out, A);
  not not_3 (not_3_out, i);
  not not_4 (not_4_out, B);
  not not_5 (not_5_out, i);
  not not_6 (not_6_out, D);
  not not_7 (not_7_out, B);
  not not_8 (not_8_out, C);
  not not_9 (not_9_out, A);
  not not_10 (not_10_out, B);
  not not_11 (not_11_out, C);
  not not_12 (not_12_out, D);
  and and_1 (and_1_out, not_1_out, not_2_out, B, C, D);
  and and_2 (and_2_out, not_3_out, A, not_4_out);
  and and_3 (and_3_out, not_5_out, A, not_6_out);
  and and_4 (and_4_out, A, not_7_out, D);
  and and_5 (and_5_out, A, B, not_8_out);
  and and_6 (and_6_out, i, not_9_out, not_10_out, not_11_out, not_12_out);
  and and_7 (and_7_out, i, A, C);
  or or_1 (DA, and_1_out, and_2_out, and_3_out, and_4_out, and_5_out, and_6_out, and_7_out);
endmodule

module DB (
  input  i,
  input  A,
  input  B,
  input  C,
  input  D,
  output DB
);

  wire and_1_out, and_2_out, and_3_out, and_4_out, and_5_out, not_1_out, not_2_out, not_3_out, not_4_out,
       not_5_out, not_6_out, not_7_out, not_8_out;

  not not_1 (not_1_out, i);
  not not_2 (not_2_out, B);
  not not_3 (not_3_out, i);
  not not_4 (not_4_out, C);
  not not_5 (not_5_out, D);
  not not_6 (not_6_out, B);
  not not_7 (not_7_out, C);
  not not_8 (not_8_out, D);
  and and_1 (and_1_out, not_1_out, not_2_out, C, D);
  and and_2 (and_2_out, not_3_out, B, not_4_out);
  and and_3 (and_3_out, B, C, not_5_out);
  and and_4 (and_4_out, i, not_6_out, not_7_out, not_8_out);
  and and_5 (and_5_out, i, B, D);
  or or_1 (DB, and_1_out, and_2_out, and_3_out, and_4_out, and_5_out);
endmodule

module DC (
  input  i,
  input  A,
  input  B,
  input  C,
  input  D,
  output DC
);

  wire and_1_out, and_2_out, and_3_out, and_4_out, not_1_out, not_2_out, not_3_out, not_4_out, not_5_out,
       not_6_out;

  not not_1 (not_1_out, i);
  not not_2 (not_2_out, C);
  not not_3 (not_3_out, i);
  not not_4 (not_4_out, D);
  not not_5 (not_5_out, C);
  not not_6 (not_6_out, D);
  and and_1 (and_1_out, not_1_out, not_2_out, D);
  and and_2 (and_2_out, not_3_out, C, not_4_out);
  and and_3 (and_3_out, i, not_5_out, not_6_out);
  and and_4 (and_4_out, i, C, D);
  or or_1 (DC, and_1_out, and_2_out, and_3_out, and_4_out);
endmodule

module DD (
  input  i,
  input  A,
  input  B,
  input  C,
  input  D,
  output DD
);

  not not_1 (DD, D);
endmodule

module Counter_8_bit (
  input  in_1,
  output out_2,
  output out_3,
  output out_4,
  output out_5,
  output out_6,
  output out_7,
  output out_8,
  output out_9
);

  wire clock_1_out, undriven;

  Clock clock_1 (.out(clock_1_out));
  Counter_4_bit counter_4_bit_1 (.i(in_1), .Clock(undriven), .A(out_2), .B(out_3), .C(out_4), .D(out_5));
  Counter_4_bit counter_4_bit_2 (.i(in_1), .Clock(clock_1_out), .A(out_6), .B(out_7), .C(out_8), .D(out_9));
endmodule
